# Fritzing sketch Smart Bluetooth Gateway Observer (saved by Fritzing 0.9.9b)
breadboards: 1

parts:
  Argon = Particle Argon
  OLED_Display = OLED 128x64 I2C Monochrome Display
  Button = Pushbutton [package="[THT]"]
  GPS_Module = u-blox NEO-6M GPS Breakout

nets:
  3.3V: Argon.3.3V, OLED_Display.VDD, GPS_Module.VCC
  GND: Argon.GND, OLED_Display.GND, Button.Pin_3, Button.Pin_4, GPS_Module.GND
  N1: Argon.A1, Button.Pin_1, Button.Pin_2
  N2: Argon.RX, GPS_Module.TXD
  N3: Argon.TX, GPS_Module.RXD
  N4: Argon.SDA, OLED_Display.SDA
  N5: Argon.SCL, OLED_Display.SCK

notes:
  Smart Bluetooth Gateway

custom parts:
  Particle Argon: The Argon is a powerful Wi-Fi enabled development board that can act as either a standalone Wi-Fi endpoint or Wi-Fi enabled gateway for Particle Mesh networks. It is based on the Nordic nRF52840 and has built-in battery charging circuitry so it’s easy to connect a Li-Po and deploy your local network in minutes. The Argon is great for connecting existing projects to the Particle Device Cloud or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
  Pushbutton: A generic pushbutton.
